# Fritzing sketch Huddle System (saved by Fritzing 0.9.2b)
breadboards: 1

parts:
  PIR1 = PIR sensor
  LED1 = smd LED [color="Red (633nm)" package="0805 [SMD]"]
  Huddle_1 = Huddle [package="DIP (Dual Inline) [THT]"]
  Moteino1 = 36 [package="DIP (Dual Inline) [THT]"]

nets:
  VDD: PIR1.VDD, Huddle_1.PWR, Moteino1.VIN
  N1: PIR1.SIG, LED1.anode, Moteino1.3
  GND: PIR1.GND, Huddle_1.GND, Moteino1.GND

custom parts:
  Huddle: Huddle Case
  36: ATmega328
